// Logisim project half_adder.circ as structural Verilog: 1 circuit, main circuit main
module main (
  input  A,
  input  B,
  output Result___A_xor_B,
  output Carry___A_and_B
);

  xor xor_1 (Result___A_xor_B, B, A);
  and and_1 (Carry___A_and_B, A, B);
endmodule
