// Logisim project modb.circ as structural Verilog: 1 circuit, main circuit main
module main (
  input  C0,
  input  C1,
  input  B,
  output out_4
);

  wire and_1_out, and_2_out;

  and and_1 (and_1_out, ~C0, B);  // AND_Gate
  and and_2 (and_2_out, C1, ~B);  // AND_Gate
  or or_1 (out_4, and_1_out, and_2_out);
endmodule
