// Logisim project somador2bits.circ as structural Verilog: 1 circuit, main circuit main
module main (
  input  A,
  input  B,
  input  A_2,
  input  B_2,
  input  CarryIn,
  output Result___A_xor_B,
  output Carry___A_and_B,
  output Result,
  output CarryOut
);

  wire and_2_out, and_3_out, xor_2_out;

  xor xor_1 (Result___A_xor_B, B, A);
  and and_1 (Carry___A_and_B, A, B);
  xor xor_2 (xor_2_out, A_2, B_2);
  and and_2 (and_2_out, xor_2_out, CarryIn);
  and and_3 (and_3_out, B_2, A_2);
  xor xor_3 (Result, xor_2_out, CarryIn);
  or or_1 (CarryOut, and_2_out, and_3_out);
endmodule
